// Logisim project IT012_Lab01_25520412.circ as structural Verilog: 6 circuits, main circuit TN1
module TN1 (
  input  A,
  input  B,
  input  C,
  output x,
  output y,
  output z,
  output u,
  output v,
  output w,
  output s,
  output XOR3,
  output NAND3,
  output CHAIN
);

  wire nand_1_out;

  not not_1 (x, A);
  nand nand_1 (nand_1_out, A, B);
  and and_1 (y, A, B);
  or or_1 (z, A, B);
  nand nand_2 (u, A, B);
  nor nor_1 (v, A, B);
  xor xor_1 (w, A, B);
  ExactlyOne xor_2 (.out(XOR3), .in0(A), .in1(B), .in2(C));
  xnor xnor_1 (s, A, B);
  nand nand_3 (NAND3, A, B, C);
  nand nand_4 (CHAIN, nand_1_out, C);
endmodule

module TN2 (
  input  x,
  input  y,
  input  z,
  output EQ1,
  output EQ2,
  output EQ3,
  output EQ4,
  output EQ5
);

  wire and_1_out, and_2_out, and_3_out, and_4_out, nand_1_out, nor_1_out, not_1_out, not_2_out, or_1_out,
       or_2_out, or_3_out, or_4_out, or_5_out;

  not not_1 (not_1_out, x);
  not not_2 (not_2_out, y);
  and and_1 (and_1_out, y, z);
  or or_1 (or_1_out, x, y);
  or or_2 (or_2_out, x, z);
  or or_3 (or_3_out, x, y);
  nand nand_1 (nand_1_out, x, y);
  or or_4 (or_4_out, x, and_2_out);
  and and_2 (and_2_out, not_1_out, y);
  nor nor_1 (nor_1_out, x, y);
  and and_3 (and_3_out, not_1_out, not_2_out);
  or or_5 (or_5_out, x, and_1_out);
  and and_4 (and_4_out, or_1_out, or_2_out);
  xnor xnor_1 (EQ1, nor_1_out, and_3_out);
  xnor xnor_2 (EQ2, nand_1_out, and_3_out);
  xnor xnor_3 (EQ3, or_5_out, and_4_out);
  xnor xnor_4 (EQ4, or_4_out, x);
  xnor xnor_5 (EQ5, or_4_out, or_3_out);
endmodule

module TN3 (
  input  A,
  input  B,
  input  C,
  input  D,
  output F
);

  wire and_1_out, and_2_out, and_3_out, and_4_out, and_5_out, and_6_out, not_1_out, not_2_out, not_3_out,
       not_4_out;

  not not_1 (not_1_out, A);
  not not_2 (not_2_out, B);
  not not_3 (not_3_out, C);
  not not_4 (not_4_out, D);
  and and_1 (and_1_out, not_1_out, not_2_out, C, not_4_out);
  and and_2 (and_2_out, not_1_out, not_2_out, C, D);
  and and_3 (and_3_out, not_1_out, B, not_3_out, D);
  and and_4 (and_4_out, not_1_out, B, C, D);
  and and_5 (and_5_out, A, not_2_out, C, D);
  and and_6 (and_6_out, A, B, not_3_out, D);
  or or_1 (F, and_1_out, and_2_out, and_3_out, and_4_out, and_5_out, and_6_out);
endmodule

module TN4 (
  input  A,
  input  B,
  input  C,
  input  D,
  output Fcan,
  output EQ1,
  output F_sop,
  output EQ2,
  output F_pos
);

  wire and_1_out, and_2_out, and_3_out, and_4_out, and_5_out, and_6_out, and_7_out, and_8_out, and_9_out,
       and_10_out, not_1_out, not_2_out, not_3_out, not_4_out, or_1_out, or_2_out, or_3_out, or_4_out;

  not not_1 (not_1_out, A);
  not not_2 (not_2_out, B);
  not not_3 (not_3_out, C);
  not not_4 (not_4_out, D);
  or or_1 (or_1_out, B, C);
  or or_2 (or_2_out, not_2_out, D);
  or or_3 (or_3_out, not_1_out, D);
  or or_4 (or_4_out, not_1_out, not_2_out, not_3_out);
  and and_1 (and_1_out, not_1_out, not_2_out, C, not_4_out);
  and and_2 (and_2_out, not_1_out, not_2_out, C, D);
  and and_3 (and_3_out, not_1_out, B, not_3_out, D);
  and and_4 (and_4_out, not_1_out, B, C, D);
  and and_5 (and_5_out, A, not_2_out, C, D);
  and and_6 (and_6_out, A, B, not_3_out, D);
  and and_7 (and_7_out, not_1_out, not_2_out, C);
  and and_8 (and_8_out, B, not_3_out, D);
  and and_9 (and_9_out, not_2_out, C, D);
  and and_10 (and_10_out, not_1_out, B, D);
  or or_5 (Fcan, and_1_out, and_2_out, and_3_out, and_4_out, and_5_out, and_6_out);
  or or_6 (F_sop, and_7_out, and_8_out, and_9_out, and_10_out);
  and and_11 (F_pos, or_1_out, or_2_out, or_3_out, or_4_out);
  xnor xnor_1 (EQ1, Fcan, F_sop);
  xnor xnor_2 (EQ2, F_sop, F_pos);
endmodule

module TN5 (
  input  A,
  input  B,
  input  C,
  output FD
);

  wire xor_1_out;

  xor xor_1 (xor_1_out, A, B);
  xor xor_2 (FD, xor_1_out, C);
endmodule

module WarmUp (
  input  A,
  input  B,
  output F
);

  wire not_1_out;

  not not_1 (not_1_out, B);
  and and_1 (F, A, not_1_out);
endmodule
