// Logisim project IT012_Lab02_25520412.circ as structural Verilog: 10 circuits, main circuit ADDSUB4
module LT (
  input  A7,
  input  B7,
  input  R7,
  output outLT
);

  wire and_1_out, and_2_out, and_3_out, not_1_out;

  not not_1 (not_1_out, B7);
  and and_1 (and_1_out, A7, not_1_out);
  and and_2 (and_2_out, A7, R7);
  and and_3 (and_3_out, not_1_out, R7);
  or or_1 (outLT, and_1_out, and_2_out, and_3_out);
endmodule

module Warmup (
  input  [7:0] A,
  input  [7:0] B,
  output [7:0] S
);

  Adder adder_1 (.a(A), .b(B), .out(S));  // open: cin, cout
  // Probe on S
  // Probe on S
endmodule

module FA (
  input  A,
  input  B,
  input  Cin,
  output S,
  output Cout
);

  wire and_1_out, and_2_out, xor_1_out;

  xor xor_1 (xor_1_out, A, B);
  and and_1 (and_1_out, B, A);
  and and_2 (and_2_out, xor_1_out, Cin);
  xor xor_2 (S, xor_1_out, Cin);
  or or_1 (Cout, and_2_out, and_1_out);
endmodule

module ADDSUB4 (
  input  [3:0] A,
  input  SUB,
  input  [3:0] B,
  output [3:0] S,
  output C
);

  wire FA0_cout, FA1_cout, FA2_cout, xor_1_out, xor_2_out, xor_3_out, xor_4_out;

  xor xor_1 (xor_1_out, B[0], SUB);
  xor xor_2 (xor_2_out, B[1], SUB);
  xor xor_3 (xor_3_out, B[2], SUB);
  xor xor_4 (xor_4_out, B[3], SUB);
  FA FA0 (.A(A[0]), .B(xor_1_out), .Cin(SUB), .S(S[0]), .Cout(FA0_cout));
  // Probe on FA0_cout
  FA FA1 (.A(A[1]), .B(xor_2_out), .Cin(FA0_cout), .S(S[1]), .Cout(FA1_cout));
  // Probe on FA1_cout
  FA FA2 (.A(A[2]), .B(xor_3_out), .Cin(FA1_cout), .S(S[2]), .Cout(FA2_cout));
  // Probe on FA2_cout
  FA FA3 (.A(A[3]), .B(xor_4_out), .Cin(FA2_cout), .S(S[3]), .Cout(C));
endmodule

module ALU8 (
  input  [2:0] OP,
  input  [7:0] A,
  input  [7:0] B,
  output [7:0] R,
  output Z,
  output out_LT
);

  wire [7:0] adder_1_out, adder_2_out, and_1_out, multiplexer_1_out, multiplexer_2_out, not_1_out, or_1_out,
       subtractor_1_out, subtractor_2_out, xor_1_out;

  Adder adder_1 (.a(A), .b(B), .out(adder_1_out));  // open: cin, cout
  Adder adder_2 (.a(A), .b(8'h1), .out(adder_2_out));  // open: cin, cout
  Subtractor subtractor_1 (.a(A), .b(B), .out(subtractor_1_out));  // open: bin, bout
  Subtractor subtractor_2 (.a(A), .b(8'h1), .out(subtractor_2_out));  // open: bin, bout
  assign and_1_out = A & B;  // AND_Gate and_1, 8 bits wide
  assign or_1_out = A | B;  // OR_Gate or_1, 8 bits wide
  assign not_1_out = ~A;  // NOT_Gate not_1, 8 bits wide
  assign xor_1_out = A ^ B;  // XOR_Gate xor_1, 8 bits wide
  Multiplexer #(.select(2), .width(8)) multiplexer_1 (
    .in0(adder_1_out), .in1(adder_2_out), .in2(subtractor_1_out), .in3(subtractor_2_out),
    .out(multiplexer_1_out), .sel(OP[1:0]));
  Multiplexer #(.select(2), .width(8)) multiplexer_2 (
    .in0(and_1_out), .in1(or_1_out), .in2(not_1_out), .in3(xor_1_out), .out(multiplexer_2_out));  // open: sel
  Multiplexer #(.width(8)) multiplexer_3 (.in0(multiplexer_1_out), .in1(multiplexer_2_out), .out(R), .sel(OP[2]));
  nor nor_1 (Z, R[0], R[1], R[2], R[3], R[4], R[5], R[6], R[7]);
  LT lt_1 (.A7(A[7]), .B7(B[7]), .R7(R[7]), .outLT(out_LT));
endmodule

module DLATCH (
  input  E,
  input  D,
  output Q
);

  Multiplexer multiplexer_1 (.in0(Q), .in1(D), .out(Q), .sel(E));
endmodule

module DFF_MS (
  input  CLK,
  input  D,
  output Q
);

  wire MASTER_q, not_1_out;

  not not_1 (not_1_out, CLK);
  DLATCH MASTER (.E(not_1_out), .D(D), .Q(MASTER_q));
  DLATCH SLAVE (.E(CLK), .D(MASTER_q), .Q(Q));
endmodule

module TN3 (
  input  CLK,
  input  D,
  output Q1,
  output Q2,
  output Q3,
  output QL2,
  output QL1,
  output QF2,
  output QF1
);

  D_Flip_Flop d_ff_1 (.D(D), .clk(CLK), .Q(Q2));  // open: Qn, preset, reset
  D_Flip_Flop d_ff_2 (.D(D), .clk(CLK), .Q(QF1));  // open: Qn, preset, reset
  D_Flip_Flop d_ff_3 (.D(QF1), .clk(CLK), .Q(QF2));  // open: Qn, preset, reset
  DLATCH dlatch_1 (.E(CLK), .D(D), .Q(Q1));
  DFF_MS dff_ms_1 (.CLK(CLK), .D(D), .Q(Q3));
  DLATCH dlatch_2 (.E(CLK), .D(D), .Q(QL1));
  DLATCH dlatch_3 (.E(CLK), .D(QL1), .Q(QL2));
endmodule

module REGFILE (
  input  [7:0] DIN,
  input  CLK,
  input  WE,
  input  [1:0] RD,
  input  [1:0] RA,
  input  [1:0] RB,
  output [7:0] R0,
  output [7:0] QA,
  output [7:0] R1,
  output [7:0] R2,
  output [7:0] QB,
  output [7:0] R3
);

  wire decoder_1_out0, decoder_1_out1, decoder_1_out2, decoder_1_out3;

  Decoder #(.select(2)) decoder_1 (
    .out0(decoder_1_out0), .out1(decoder_1_out1), .out2(decoder_1_out2), .out3(decoder_1_out3), .sel(RD),
    .en(WE));
  Register register_1 (.D(DIN), .en(decoder_1_out0), .clk(CLK), .Q(R0));  // open: clr
  Register register_2 (.D(DIN), .en(decoder_1_out1), .clk(CLK), .Q(R1));  // open: clr
  Register register_3 (.D(DIN), .en(decoder_1_out2), .clk(CLK), .Q(R2));  // open: clr
  Register register_4 (.D(DIN), .en(decoder_1_out3), .clk(CLK), .Q(R3));  // open: clr
  Multiplexer #(.select(2), .width(8)) multiplexer_1 (.in0(R0), .in1(R1), .in2(R2), .in3(R3), .out(QA), .sel(RA));
  Multiplexer #(.select(2), .width(8)) multiplexer_2 (.in0(R0), .in1(R1), .in2(R2), .in3(R3), .out(QB), .sel(RB));
endmodule

module DATAPATH (
  input  [7:0] IMM,
  input  SRC,
  input  CLK,
  input  WE,
  input  [1:0] RD,
  input  [1:0] RA,
  input  [1:0] RB,
  input  [2:0] OP,
  output [7:0] R0,
  output [7:0] R1,
  output [7:0] R2,
  output [7:0] R3,
  output [7:0] R,
  output Z
);

  wire [7:0] multiplexer_1_out, regfile_1_qa, regfile_1_qb;

  Multiplexer #(.enable("true"), .width(8)) multiplexer_1 (
    .in0(R), .in1(IMM), .out(multiplexer_1_out), .sel(SRC));  // open: en
  REGFILE regfile_1 (
    .DIN(multiplexer_1_out), .CLK(CLK), .WE(WE), .RD(RD), .RA(RA), .RB(RB), .R0(R0), .QA(regfile_1_qa),
    .R1(R1), .R2(R2), .QB(regfile_1_qb), .R3(R3));
  ALU8 alu8_1 (.OP(OP), .A(regfile_1_qa), .B(regfile_1_qb), .R(R), .Z(Z));  // open: out_LT
endmodule
